# Fritzing sketch Low-side transistor switch (saved by Fritzing 0.9.6b)
breadboards: 1

parts:
  Espessif_Serial_Wifi_Modul_1 = ESP8266 ESP01 [part_number=ESP8266 package=THT]
  BAT1 = Battery Holders [part_number=3.3v package=lipo-1100mAh]
  R1 = Resistor [tolerance=±5% power=0.25 resistance=10k package=THT]
  Q1 = NPN-Transistor [part_number=2n2222 package="TO92 [THT]"]
  R2 = Resistor [tolerance=±5% power=0.25 resistance=5k package=THT]
  U2 = RELAY-SOLIDSTATE [part_number="JGX-1 D4810A 10A, DC - AC" package=relay-s108t02]
  V1 = AC Power [voltage=220 frequency=50]
  LED1 = LEDs [part_number=AC package=led10mm]
  R3 = Resistor [tolerance=±5% power=0.25 resistance=10k package=THT]

nets (from the schematic view):
  N1: Espessif_Serial_Wifi_Modul_1.GND, BAT1.-, Q1.E
  N2: Espessif_Serial_Wifi_Modul_1.VCC, BAT1.+, R1.Pin_0, U2.+, R3.Pin_0
  N3: Espessif_Serial_Wifi_Modul_1.GPIO00, R1.Pin_1
  N4: Espessif_Serial_Wifi_Modul_1.GPIO02, R2.Pin_0, R3.Pin_1
  N5: Q1.B, R2.Pin_1
  N6: Q1.C, U2.-
  N7: U2.T1, V1.V-
  N8: U2.T2, LED1.C
  N9: V1.V+, LED1.A

custom parts:
  ESP8266 ESP01: Generic WiFi Module based on the ESP8266 with onboard PCB antenna and UART communications
  LEDs: LEDs Standard schematic elements and footprints for 5mm, 3mm, 1206, and 0603 sized LEDs. 5mm - Spark Fun Electronics SKU : COM-00529 (and others)
